# Fritzing sketch breadboard-prototype (saved by Fritzing 0.9.9b)
circuit board: 6.34892cm x 5.88749cm
breadboards: 1

parts:
  HC-SR04_Sensor_1 = HC-SR04 Ultrasonic Distance Sensor
  U1 = LuaNode32 / ESP32 [part_number=ESP32S-PIN30]
  U3 = 2-Channel 5v Relay Shield [package=relay-2ch5v10a]

nets:
  VCC: HC-SR04_Sensor_1.VCC, U1.Vin, U3.VCC
  N1: HC-SR04_Sensor_1.TRIG, U1.D26
  N2: HC-SR04_Sensor_1.ECHO, U1.D25
  GND: HC-SR04_Sensor_1.GND, U1.GND, U3.GND
  N3: U1.D18, U3.IN2
  N4: U1.D19, U3.IN1

notes:
  Relay

custom parts:
  LuaNode32 / ESP32: New Image for LuaNode32 DOIT ESP32 DEVKIT V1. Base parts from LuaNode32 / ESP32 ESP32 based LuaNode32 by G.Noorlander DOIT Esp32 DevKit v1 (30 pins long, 11 pins width) by Werner Rothschopf (modified by vanepp Dec 2018)
  2-Channel 5v Relay Shield: 2 Channel 5v Relay Shield w. 2x SPD-06VDC-SD-C
